// Logisim project ex1.circ as structural Verilog: 2 circuits, main circuit main
module main (
  input  A,
  input  B
);

  wire and_1_out, nand_1_out, or_1_out;

  or or_1 (or_1_out, A, B);
  nand nand_1 (nand_1_out, A, B);
  and and_1 (and_1_out, or_1_out, nand_1_out);
  // Probe on and_1_out
endmodule

module NOR (
  input  A,
  input  B,
  output S
);

  wire nand_1_out, or_1_out;

  or or_1 (or_1_out, A, B);
  nand nand_1 (nand_1_out, A, B);
  and and_1 (S, or_1_out, nand_1_out);
endmodule
