// Logisim project ex2.circ as structural Verilog
module add1 (
  input  A,
  input  B,
  output S,
  output Rs
);

  and and_1 (S, A, B);
  or or_1 (Rs, A, B);
endmodule

module add1r (
  input  A,
  input  B,
  input  Re,
  output S,
  output Rs
);

  wire add1_1_rs, add1_1_s, add1_2_rs;

  add1 add1_1 (.A(A), .B(B), .S(add1_1_s), .Rs(add1_1_rs));
  add1 add1_2 (.A(add1_1_s), .B(Re), .S(S), .Rs(add1_2_rs));
  or or_1 (Rs, add1_2_rs, add1_1_rs);
endmodule
