// Logisim project ex1.circ as structural Verilog
module registre8bits (
  input  C,
  input  D,
  input  E,
  input  F,
  input  G,
  input  H,
  input  B,
  input  A,
  input  CLOCK,
  output S2,
  output S3,
  output S4,
  output S5,
  output S6,
  output S7,
  output S1,
  output S8
);

  wire boited_1_r, boited_1_s, boited_2_r, boited_2_s, boited_3_r, boited_3_s, boited_4_r, boited_4_s,
       boited_5_r, boited_5_s, boited_6_r, boited_6_s, boited_7_r, boited_7_s, boited_8_r, boited_8_s;

  boiteD boited_1 (.A(A), .S(boited_1_s), .R(boited_1_r));
  boiteD boited_2 (.A(B), .S(boited_2_s), .R(boited_2_r));
  S_R_Flip_Flop s_r_ff_1 (.S(boited_1_s), .clk(CLOCK), .R(boited_1_r), .Q(S1));  // open: Qn, preset, reset, en
  boiteD boited_3 (.A(C), .S(boited_3_s), .R(boited_3_r));
  S_R_Flip_Flop s_r_ff_2 (.S(boited_2_s), .clk(CLOCK), .R(boited_2_r), .Q(S2));  // open: Qn, preset, reset, en
  boiteD boited_4 (.A(D), .S(boited_4_s), .R(boited_4_r));
  S_R_Flip_Flop s_r_ff_3 (.S(boited_3_s), .clk(CLOCK), .R(boited_3_r), .Q(S3));  // open: Qn, preset, reset, en
  boiteD boited_5 (.A(E), .S(boited_5_s), .R(boited_5_r));
  S_R_Flip_Flop s_r_ff_4 (.S(boited_4_s), .clk(CLOCK), .R(boited_4_r), .Q(S4));  // open: Qn, preset, reset, en
  S_R_Flip_Flop s_r_ff_5 (.S(boited_5_s), .clk(CLOCK), .R(boited_5_r), .Q(S5));  // open: Qn, preset, reset, en
  boiteD boited_6 (.A(F), .S(boited_6_s), .R(boited_6_r));
  S_R_Flip_Flop s_r_ff_6 (.S(boited_6_s), .clk(CLOCK), .R(boited_6_r), .Q(S6));  // open: Qn, preset, reset, en
  boiteD boited_7 (.A(G), .S(boited_7_s), .R(boited_7_r));
  boiteD boited_8 (.A(H), .S(boited_8_s), .R(boited_8_r));
  S_R_Flip_Flop s_r_ff_7 (.S(boited_7_s), .clk(CLOCK), .R(boited_7_r), .Q(S7));  // open: Qn, preset, reset, en
  S_R_Flip_Flop s_r_ff_8 (.S(boited_8_s), .clk(CLOCK), .R(boited_8_r), .Q(S8));  // open: Qn, preset, reset, en
endmodule

module boiteD (
  input  A,
  output S,
  output R
);

  not not_1 (R, A);

  assign S = A;
endmodule

module add8bits (
  input  [7:0] A,
  input  A_prime,
  input  B_prime,
  input  C_prime,
  input  D_prime,
  input  E_prime,
  input  SEL,
  input  F_prime,
  input  G_prime,
  input  H_prime,
  input  CLOCK,
  input  [7:0] B,
  output [7:0] S,
  output R
);

  wire [7:0] multiplexer_1_out, registre8bits_1_s2;

  registre8bits registre8bits_1 (
    .C(A_prime), .D(B_prime), .E(C_prime), .F(D_prime), .G(E_prime), .H(F_prime), .B(G_prime), .A(H_prime),
    .CLOCK(CLOCK), .S2(registre8bits_1_s2[0]), .S3(registre8bits_1_s2[1]), .S4(registre8bits_1_s2[2]),
    .S5(registre8bits_1_s2[3]), .S6(registre8bits_1_s2[4]), .S7(registre8bits_1_s2[5]),
    .S1(registre8bits_1_s2[6]), .S8(registre8bits_1_s2[7]));
  Multiplexer #(.width(8)) multiplexer_1 (
    .in0(A), .in1(registre8bits_1_s2), .out(multiplexer_1_out), .sel(SEL));  // open: en
  Adder adder_1 (.a(multiplexer_1_out), .b(B), .out(S), .cout(R));  // open: cin
endmodule

module complementA2 (
  input  [7:0] A,
  output [7:0] S
);

  wire [7:0] complementa1_1_s;

  complementA1 complementa1_1 (.A(A), .S(complementa1_1_s));
  Adder adder_1 (.a(complementa1_1_s), .b(8'h1), .out(S));  // open: cin, cout
endmodule

module complementA1 (
  input  [7:0] A,
  output [7:0] S
);

  assign S = ~A;  // NOT_Gate not_1, 8 bits wide
endmodule

module add_sous8bits (
  input  [7:0] A,
  input  A_prime,
  input  B_prime,
  input  C_prime,
  input  D_prime,
  input  E_prime,
  input  SEL,
  input  F_prime,
  input  G_prime,
  input  H_prime,
  input  CLOCK,
  input  [7:0] B,
  input  SOUSTRACTION,
  output [7:0] S,
  output R
);

  wire [7:0] complementa2_1_s, multiplexer_1_out, multiplexer_2_out, registre8bits_1_s2;

  registre8bits registre8bits_1 (
    .C(A_prime), .D(B_prime), .E(C_prime), .F(D_prime), .G(E_prime), .H(F_prime), .B(G_prime), .A(H_prime),
    .CLOCK(CLOCK), .S2(registre8bits_1_s2[0]), .S3(registre8bits_1_s2[1]), .S4(registre8bits_1_s2[2]),
    .S5(registre8bits_1_s2[3]), .S6(registre8bits_1_s2[4]), .S7(registre8bits_1_s2[5]),
    .S1(registre8bits_1_s2[6]), .S8(registre8bits_1_s2[7]));
  complementA2 complementa2_1 (.A(B), .S(complementa2_1_s));
  Multiplexer #(.width(8)) multiplexer_1 (
    .in0(A), .in1(registre8bits_1_s2), .out(multiplexer_1_out), .sel(SEL));  // open: en
  Multiplexer #(.width(8)) multiplexer_2 (
    .in0(B), .in1(complementa2_1_s), .out(multiplexer_2_out), .sel(SOUSTRACTION));  // open: en
  Adder adder_1 (.a(multiplexer_1_out), .b(multiplexer_2_out), .out(S), .cout(R));  // open: cin

  // Notes on the sheet:
  //   +B
  //   -B
endmodule
