// Logisim project ex2.circ as structural Verilog
module diagrammeEtat (
  input  _000,
  input  _001,
  input  _011,
  input  _010,
  input  _100,
  input  _110,
  input  _101,
  input  _111
);


  // Notes on the sheet:
  //   e=0
  //   e=0
  //   Diagramme d'état - exercice 2
  //   e=0
  //   \/
  //   e=1
  //   \/
  //   e=1
  //   /\
  //   \/
  //   <
  //   <
  //   >
  //   \/
  //   \/
  //   e=1
  //   <
  //   >
  //   e=0
  //   e=1
  //   e=0
  //   e=0 ou 1
  //   e=1
  //   e=0
  //   \/
  //   >
  //   \/
  //   e=1
  //   e=0 ou 1
  //   Me suis fait chier mais c'est boooooo =)
endmodule
